# Fritzing sketch MLSA_I2C (saved by Fritzing 0.9.3b)
breadboards: 2

parts:
  LCD2004-I2C1 = LCD2004-I2C
  U1 = NodeMCU V3.0
  BAT1 = BC9VPC [package=bc9vpc]
  BAT2 = BC9VPC [package=bc9vpc]
  KY-1 = Keyes Relay [package=THT]
  hc-sr1 = hc-sr04
  M1 = DC Motor
  IC1 = Voltage Regulator [package=to-220-alt]
  IC2 = Voltage Regulator [package=to-220-alt]

nets:
  GND: LCD2004-I2C1.GND, U1.GND, BAT1.V-, KY-1.ground, hc-sr1.GND, IC2.IN
  VCC: LCD2004-I2C1.VCC, hc-sr1.VCC, IC2.OUT
  N1: LCD2004-I2C1.SDA, U1.D4
  N2: LCD2004-I2C1.SCL, U1.D3
  N3: U1.D0, hc-sr1.Trig
  N4: U1.D1, hc-sr1.Echo
  N5: U1.3V3, KY-1.power
  N6: BAT1.V+, IC2.GND
  N7: BAT2.V+, IC1.GND
  N8: BAT2.V-, M1.pin_2, IC1.IN
  N9: KY-1.NC, KY-1.C, IC1.OUT
  N10: KY-1.NO, M1.pin_1

custom parts:
  LCD2004-I2C: A standard character display with 4x20 characters. Comes in many colors with LCM2004 IIC attached.
  NodeMCU V3.0: ESP8266 based NodeMCU
  Keyes Relay: The Keyes 5V relay module is suitable for SCM development, home appliance control. It uses a 5V~12V TIL control signal which can control DC / AC signal.
